# Fritzing sketch Fritzing_simüasyonu (saved by Fritzing 0.9.4)
breadboards: 1

parts:
  J3 = Basic Servo
  J4 = Basic Servo
  R9 = Photocell (LDR) [package=THT]
  R10 = Photocell (LDR) [package=THT]
  R11 = Photocell (LDR) [package=THT]
  R12 = Photocell (LDR) [package=THT]
  R13 = Resistor [tolerance=±5% resistance=220 package=THT]
  R14 = Resistor [tolerance=±5% resistance=220 package=THT]
  R15 = Resistor [tolerance=±5% resistance=220 package=THT]
  R16 = Resistor [tolerance=±5% resistance=220 package=THT]
  Teensy2 = Teensy 3.6 (Basic)
  S1 = Pushbutton [package="[SMD]"]
  R17 = Resistor [tolerance=±5% resistance=220 package="0402 [SMD]"]

nets:
  GND: J3.gnd, J4.gnd, R13.Pin_1, R14.Pin_1, R15.Pin_1, R16.Pin_1, Teensy2.GND, Teensy2.GND1, R17.Pin_1
  VCC: J3.vcc, J4.vcc, R9.pin_1, R10.pin_1, R11.pin_1, R12.pin_1, Teensy2.3V3
  N1: J3.pulse, Teensy2.D9
  N2: J4.pulse, Teensy2.D10
  N3: R9.pin_0, R13.Pin_0, Teensy2.A3/D17
  N4: R10.pin_0, R14.Pin_0, Teensy2.A2/D16
  N5: R11.pin_0, R15.Pin_0, Teensy2.A1/D15
  N6: R12.pin_0, R16.Pin_0, Teensy2.A0/D14
  N7: Teensy2.D3, S1.Pin_1, S1.Pin_2, R17.Pin_0
  N8: S1.Pin_3, S1.Pin_4

notes:
  eem419_Grp_II_11_İki_Ekseli_Hareket_ile_Güneş_Takibi_yapan_solar_panel

custom parts:
  Teensy 3.6 (Basic): The Teensy is a complete USB-based microcontoller development system, in a very small footprint, capable of implementing many types of projects. All programming is done via the USB port. No special programmer is needed, only a standard micro-USB cable and a PC or Macintosh with a USB port.
